# Fritzing sketch wiring (saved by Fritzing 0.9.6b)
perfboards: 1

parts:
  Grove1 = Grove OLED 128x96
  BATT1 = 3xAAA Switchable Battery Pack w/Bare Wire
  A1 = Waveshare rp2040-zero tht [package=THT]
  U1 = HALL-EFFECT [package=sc70]
  S1 = SWITCH-DPDT [package=mss22]
  J2 = female pin header, 2 pins [form="♀ (female)"]
  J3 = female pin header, 2 pins [form="♀ (female)"]
  J4 = JST XH_2.54mm Horizontal SMD Connector 3pin [package=SMD]
  S2 = Round Pushbutton
  J5 = female pin header, 2 pins [form="♀ (female)"]
  J6 = female pin header, 2 pins [form="♀ (female)"]

nets:
  N1: Grove1.GND, U1.OUT, J4.pin1, J6.pin2
  N2: Grove1.VCC, J6.pin1
  N3: Grove1.SDA, A1.Pin_23, J5.pin1
  N4: Grove1.SCL, A1.Pin_22, J5.pin2
  N5: BATT1.POS, S1.1
  N6: BATT1.NEG, A1.Pin_2, J2.pin2
  N7: A1.Pin_1, S1.2, J2.pin1
  N8: A1.Pin_3, U1.VCC, J4.pin2
  N9: A1.Pin_7, U1.GND, J4.pin3
  N10: A1.Pin_20, J3.pin1, S2.leg0
  N11: J3.pin2, S2.leg1

custom parts:
  3xAAA Switchable Battery Pack w/Bare Wire: 3xAAA Switchable Battery Pack w/Bare Wire Connectors
  Waveshare rp2040-zero tht: .RP2040-Zero, A Low-Cost, High-Performance Pico-Like MCU Board Based On Raspberry Pi Microcontroller RP2040. This varant is THT without the extra connections.
  JST XH_2.54mm Horizontal SMD Connector 3pin: JST XH_2.54mm Horizontal SMD Connector 3pin.
